// Digital circuit pong.dig as structural Verilog
module pong (
  input  Master_VGA_Clock,
  input  in_2,
  input  Test_Clock,
  input  in_4,
  input  in_5,
  input  Manual_Clock
);

  wire _7408_1_pin3, _7408_1_pin4, _7408_1_pin6, _7408_1_pin8, _7408_1_pin9, _7408_1_pin10, _7408_1_pin12,
       _7408_2_pin3, _7408_2_pin6, _7408_2_pin8, _7408_2_pin9, _7408_2_pin11, _7408_2_pin12, _7408_3_pin3,
       _7408_3_pin4, _7408_3_pin6, _7408_3_pin8, _7408_3_pin9, _7408_3_pin10, _7408_3_pin12, _7408_4_pin2,
       _7408_4_pin3, _7408_4_pin6, _7408_4_pin9, _7430_1_pin6, _7430_1_pin8, _7430_1_pin11, _7430_1_pin12,
       _7430_2_pin1, _7430_2_pin2, _7430_2_pin3, _7430_2_pin4, _7430_2_pin6, _7430_2_pin8, _7430_2_pin12,
       _7430_3_pin1, _7430_3_pin2, _7430_3_pin3, _7430_3_pin4, _7430_3_pin8, _7430_4_pin1, _7430_4_pin2,
       _7430_4_pin5, _7430_4_pin6, _7430_4_pin8, _7430_4_pin11, _7430_4_pin12, _7430_5_pin8, _7430_6_pin8,
       _7430_7_pin8, _7430_7_pin12, _7474_1_pin10, _7474_1_pin13, _74163_1_pin15, _74163_2_pin15,
       _74163_4_pin15, _74163_5_pin15, B, CLK, H0, H1, H2, H3, H4, H5, H6, H7, H8, H9, H10, H11, HCLR, HSYNC,
       not_7_out, not_8_out, not_13_out, not_15_out, not_28_out, not_29_out, not_30_out, not_31_out,
       not_32_out, not_33_out, not_34_out, not_43_out, not_44_out, not_45_out, not_46_out, not_47_out,
       not_48_out, not_50_out, V0, V1, V2, V3, V4, V5, V6, V7, V8, V9, V10, V11, VCLR, VSYNC;

  _74163 _74163_1 (
    .pin1(HCLR), .pin2(CLK), .pin3(1'b0), .pin4(1'b0), .pin5(1'b0), .pin6(1'b0), .pin7(1'b1), .pin8(1'b0),
    .pin9(1'b1), .pin10(1'b1), .pin11(H3), .pin12(H2), .pin13(H1), .pin14(H0), .pin15(_74163_1_pin15),
    .pin16(1'b1));
  _74163 _74163_2 (
    .pin1(HCLR), .pin2(CLK), .pin3(1'b0), .pin4(1'b0), .pin5(1'b0), .pin6(1'b0), .pin7(1'b1), .pin8(1'b0),
    .pin9(1'b1), .pin10(_74163_1_pin15), .pin11(H7), .pin12(H6), .pin13(H5), .pin14(H4),
    .pin15(_74163_2_pin15), .pin16(1'b1));
  _74163 _74163_3 (
    .pin1(HCLR), .pin2(CLK), .pin3(1'b0), .pin4(1'b0), .pin5(1'b0), .pin6(1'b0), .pin7(1'b1), .pin8(1'b0),
    .pin9(1'b1), .pin10(_74163_2_pin15), .pin11(H11), .pin12(H10), .pin13(H9), .pin14(H8), .pin16(1'b1));  // open: pin15
  // Relay #(.relayNormallyClosed("true")) relay_1: pin names not known; wires that end beside it: Master_VGA_Clock, Test_Clock, in_4, in_5, CLK
  // Relay relay_2: pin names not known; wires that end beside it: Manual_Clock, CLK
  _74163 _74163_4 (
    .pin1(VCLR), .pin2(HCLR), .pin3(1'b0), .pin4(1'b0), .pin5(1'b0), .pin6(1'b0), .pin7(1'b1), .pin8(1'b0),
    .pin9(1'b1), .pin10(1'b1), .pin11(V3), .pin12(V2), .pin13(V1), .pin14(V0), .pin15(_74163_4_pin15),
    .pin16(1'b1));
  _74163 _74163_5 (
    .pin1(VCLR), .pin2(HCLR), .pin3(1'b0), .pin4(1'b0), .pin5(1'b0), .pin6(1'b0), .pin7(1'b1), .pin8(1'b0),
    .pin9(1'b1), .pin10(_74163_4_pin15), .pin11(V7), .pin12(V6), .pin13(V5), .pin14(V4),
    .pin15(_74163_5_pin15), .pin16(1'b1));
  _74163 _74163_6 (
    .pin1(VCLR), .pin2(HCLR), .pin3(1'b0), .pin4(1'b0), .pin5(1'b0), .pin6(1'b0), .pin7(1'b1), .pin8(1'b0),
    .pin9(1'b1), .pin10(_74163_5_pin15), .pin11(V11), .pin12(V10), .pin13(V9), .pin14(V8), .pin16(1'b1));  // open: pin15
  // Relay relay_3: pin names not known; wires that end beside it: in_2, 1'b0, CLK, 1'b0, 1'b0
  VGA vga_1 (.R(B), .G(B), .B(B), .H(HSYNC), .V(VSYNC), .C(CLK));
  _7430 _7430_1 (
    .pin1(H0), .pin2(H1), .pin3(H2), .pin4(H3), .pin5(H4), .pin6(_7430_1_pin6), .pin7(1'b0),
    .pin8(_7430_1_pin8), .pin11(_7430_1_pin11), .pin12(_7430_1_pin12), .pin14(1'b1));  // open: pin9, pin10, pin13
  not not_1 (_7430_1_pin6, H5);
  _7430 _7430_2 (
    .pin1(_7430_2_pin1), .pin2(_7430_2_pin2), .pin3(_7430_2_pin3), .pin4(_7430_2_pin4), .pin5(H4),
    .pin6(_7430_2_pin6), .pin7(1'b0), .pin8(_7430_2_pin8), .pin11(H7), .pin12(_7430_2_pin12), .pin14(1'b1));  // open: pin9, pin10, pin13
  not not_2 (_7430_2_pin1, H0);
  not not_3 (_7430_2_pin2, H1);
  not not_4 (_7430_2_pin3, H2);
  not not_5 (_7430_2_pin4, H3);
  not not_6 (_7430_2_pin6, H5);
  not not_7 (not_7_out, H8);
  _7408 _7408_1 (
    .pin1(not_7_out), .pin2(H9), .pin3(_7408_1_pin3), .pin4(_7408_1_pin4), .pin5(_7408_1_pin3),
    .pin6(_7408_1_pin6), .pin7(1'b0), .pin8(_7408_1_pin8), .pin9(_7408_1_pin9), .pin10(_7408_1_pin10),
    .pin11(_7408_1_pin9), .pin12(_7408_1_pin12), .pin13(H9), .pin14(1'b1));
  not not_8 (not_8_out, _7408_1_pin6);
  _7430 _7430_3 (
    .pin1(_7430_3_pin1), .pin2(_7430_3_pin2), .pin3(_7430_3_pin3), .pin4(_7430_3_pin4), .pin5(H4), .pin6(H5),
    .pin7(1'b0), .pin8(_7430_3_pin8), .pin11(H7), .pin12(H6), .pin14(1'b1));  // open: pin9, pin10, pin13
  not not_9 (_7430_3_pin1, H0);
  not not_10 (_7430_3_pin2, H1);
  not not_11 (_7430_3_pin3, H2);
  not not_12 (_7430_3_pin4, H3);
  not not_13 (not_13_out, _7430_1_pin8);
  not not_14 (_7408_1_pin4, _7430_2_pin8);
  not not_15 (not_15_out, _7408_1_pin8);
  not not_16 (_7408_1_pin10, _7430_3_pin8);
  not not_17 (_7430_1_pin12, H7);
  not not_18 (_7430_1_pin11, H6);
  not not_19 (_7430_2_pin12, H6);
  not not_20 (_7408_1_pin12, H8);
  _7408 _7408_2 (
    .pin1(H8), .pin2(H9), .pin3(_7408_2_pin3), .pin4(not_13_out), .pin5(_7408_2_pin3), .pin6(_7408_2_pin6),
    .pin7(1'b0), .pin8(_7408_2_pin8), .pin9(_7408_2_pin9), .pin10(V9), .pin11(_7408_2_pin11),
    .pin12(_7408_2_pin12), .pin13(_7408_2_pin8), .pin14(1'b1));
  not not_21 (HCLR, _7408_2_pin6);
  _7474 _7474_1 (
    .pin1(not_8_out), .pin2(1'b0), .pin3(1'b0), .pin4(not_15_out), .pin5(HSYNC), .pin7(1'b0), .pin9(VSYNC),
    .pin10(_7474_1_pin10), .pin11(1'b0), .pin12(1'b0), .pin13(_7474_1_pin13), .pin14(1'b1));  // open: pin6, pin8
  not not_22 (VCLR, _7408_2_pin11);
  not not_23 (_7408_2_pin9, V8);
  _7430 _7430_4 (
    .pin1(_7430_4_pin1), .pin2(_7430_4_pin2), .pin3(V2), .pin4(V3), .pin5(_7430_4_pin5), .pin6(_7430_4_pin6),
    .pin7(1'b0), .pin8(_7430_4_pin8), .pin11(_7430_4_pin11), .pin12(_7430_4_pin12), .pin14(1'b1));  // open: pin9, pin10, pin13
  not not_24 (_7430_4_pin1, V0);
  not not_25 (_7430_4_pin2, V1);
  not not_26 (_7430_4_pin5, V4);
  not not_27 (_7430_4_pin6, V5);
  not not_28 (not_28_out, V0);
  not not_29 (not_29_out, V2);
  not not_30 (not_30_out, V4);
  not not_31 (not_31_out, V9);
  not not_32 (not_32_out, V0);
  not not_33 (not_33_out, V1);
  not not_34 (not_34_out, V4);
  _7430 _7430_5 (
    .pin1(not_28_out), .pin2(V1), .pin3(not_29_out), .pin4(V3), .pin5(not_30_out), .pin6(V5), .pin7(1'b0),
    .pin8(_7430_5_pin8), .pin11(V7), .pin12(V6), .pin14(1'b1));  // open: pin9, pin10, pin13
  _7408 _7408_3 (
    .pin1(V8), .pin2(not_31_out), .pin3(_7408_3_pin3), .pin4(_7408_3_pin4), .pin5(_7408_3_pin3),
    .pin6(_7408_3_pin6), .pin7(1'b0), .pin8(_7408_3_pin8), .pin9(_7408_3_pin9), .pin10(_7408_3_pin10),
    .pin11(_7408_3_pin10), .pin12(_7408_3_pin12), .pin13(V8), .pin14(1'b1));
  not not_35 (_7474_1_pin13, _7408_3_pin6);
  _7430 _7430_6 (
    .pin1(not_32_out), .pin2(not_33_out), .pin3(V2), .pin4(V3), .pin5(not_34_out), .pin6(V5), .pin7(1'b0),
    .pin8(_7430_6_pin8), .pin11(V7), .pin12(V6), .pin14(1'b1));  // open: pin9, pin10, pin13
  not not_36 (_7408_2_pin12, _7430_4_pin8);
  not not_37 (_7430_4_pin12, V7);
  not not_38 (_7430_4_pin11, V6);
  not not_39 (_7408_3_pin4, _7430_5_pin8);
  not not_40 (_7408_3_pin12, V9);
  not not_41 (_7474_1_pin10, _7408_3_pin8);
  not not_42 (_7408_3_pin9, _7430_6_pin8);
  not not_43 (not_43_out, H0);
  not not_44 (not_44_out, H1);
  not not_45 (not_45_out, H2);
  not not_46 (not_46_out, H3);
  not not_47 (not_47_out, H4);
  not not_48 (not_48_out, H5);
  _7430 _7430_7 (
    .pin1(not_43_out), .pin2(not_44_out), .pin3(not_45_out), .pin4(not_46_out), .pin5(not_47_out),
    .pin6(not_48_out), .pin7(1'b0), .pin8(_7430_7_pin8), .pin11(H6), .pin12(_7430_7_pin12), .pin14(1'b1));  // open: pin9, pin10, pin13
  not not_49 (_7430_7_pin12, H7);
  not not_50 (not_50_out, _7430_7_pin8);
  _7408 _7408_4 (
    .pin1(H8), .pin2(_7408_4_pin2), .pin3(_7408_4_pin3), .pin4(not_50_out), .pin5(_7408_4_pin3),
    .pin6(_7408_4_pin6), .pin7(1'b0), .pin8(B), .pin9(_7408_4_pin9), .pin10(_7408_4_pin6),
    .pin11(_7408_4_pin9), .pin12(V3), .pin13(1'b1), .pin14(1'b1));
  not not_51 (_7408_4_pin2, H9);

  // Other names for the same wires on the sheet: HCOUNT[9:0] = {H9, H8, H7, H6, H5, H4, H3, H2, H1, H0}; G = B; R = B

  // Notes on the sheet:
  //   Master_VGA_Clock: Hz: 25175000
  //   Test_Clock: Hz: 15
  //   COUNTERS
  //   I/O SUITE
  //   VGA DRIVER
  //   CLR
  //   SYNC GEN
  //   PARTING (STATIC)
endmodule
